# Fritzing sketch EMG5servo (saved by Fritzing 0.9.3b)
breadboards: 1

parts:
  Part2 = MyoWare Cable Shield
  Part3 = Arduino Nano (Rev3.0) (ICSP)
  J1 = Basic Servo
  J3 = Basic Servo
  J4 = Basic Servo
  J5 = Basic Servo
  J2 = Basic Servo

nets:
  VCC: Part2.VCC, J1.vcc, J3.vcc, J4.vcc, J5.vcc, J2.vcc
  GND: Part2.GND, J1.gnd, J3.gnd, J4.gnd, J5.gnd, J2.gnd
  N1: Part2.SIG, Part3.A0
  N2: Part3.D2, J1.pulse
  N3: Part3.D3, J5.pulse
  N4: Part3.D4, J4.pulse
  N5: Part3.D5, J3.pulse
  N6: Part3.D6, J2.pulse
